# Fritzing sketch Sketch (saved by Fritzing 0.9.3b)

parts:
  NANO = Arduino Nano (Rev3.0)
  OLED = OLED 128x64 I2C Monochrome Display GND-VDD
  Header1 = 2 pin header [package=THT]
  Header2 = 2 pin header [package=THT]  # not connected
  Header3 = 2 pin header [package=THT]
  Header4 = 2 pin header [package=THT]  # not connected

nets:
  GND: NANO.GND, OLED.GND, Header3.pin_1#0
  N1: NANO.D5, Header3.pin_1#1
  N2: NANO.VIN, Header1.pin_1
  N3: NANO.A5, OLED.SCK
  N4: NANO.A4, OLED.SDA
  3V3: NANO.3V3, OLED.VDD

custom parts:
  OLED 128x64 I2C Monochrome Display GND-VDD: OLED 128x64 I2C Monochrome Display. Note: there are two variants of this part, this one is the GND VDD SCK SDA variant. The other is VDD GND SCK SDA. Make sure you select the part that matches your module as using the incorrect part will probably destroy your module! In addition the mounting holes are marked on silkscreen but not by default drilled. If you want drilled mounting holes, copy a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
  2 pin header: 2 pin male to male header
